# Fritzing sketch pixelDungeon (saved by Fritzing 0.9.0b)
circuit board: 15cm x 9cm
breadboards: 5

parts:
  U5 = 74HC595 [package="DIP16 [THT]"]
  U4 = 74HC595 [package="DIP16 [THT]"]
  U3 = 74HC595 [package="DIP16 [THT]"]
  U6 = 74HC595 [package="DIP16 [THT]"]
  VCC1 = Battery block 9V
  LED1 = LED - 5mm [color="Green (570nm)" package="5 mm [THT]"]
  R31 = Resistor [tolerance=±5% resistance=220 package=THT]
  R30 = Resistor [tolerance=±5% resistance=10k package=THT]
  S1 = Pushbutton [package="[THT]"]
  C2 = Electrolytic Capacitor [capacitance=10µF package="100 mil [THT, electrolytic]"]
  C1 = Electrolytic Capacitor [capacitance=10µF package="100 mil [THT, electrolytic]"]
  S2 = Pushbutton [package="[THT]"]
  R32 = Resistor [tolerance=±5% resistance=330 package=THT]
  C12 = Tantalum Capacitor [capacitance=100nF package="100 mil [THT, tantalum]"]
  S3 = Pushbutton [package="[THT]"]
  S4 = Pushbutton [package="[THT]"]
  R35 = Resistor [tolerance=±5% resistance=330 package=THT]
  S5 = Pushbutton [package="[THT]"]
  C15 = Tantalum Capacitor [capacitance=100nF package="100 mil [THT, tantalum]"]
  S6 = Pushbutton [package="[THT]"]
  S7 = Pushbutton [package="[THT]"]
  R1 = Resistor [tolerance=±5% resistance=220 package=THT]
  R2 = Resistor [tolerance=±5% resistance=220 package=THT]
  R3 = Resistor [tolerance=±5% resistance=220 package=THT]
  R4 = Resistor [tolerance=±5% resistance=220 package=THT]
  R5 = Resistor [tolerance=±5% resistance=220 package=THT]
  R6 = Resistor [tolerance=±5% resistance=220 package=THT]
  R7 = Resistor [tolerance=±5% resistance=220 package=THT]
  R8 = Resistor [tolerance=±5% resistance=220 package=THT]
  R9 = Resistor [tolerance=±5% resistance=220 package=THT]
  R12 = Resistor [tolerance=±5% resistance=220 package=THT]
  R18 = Resistor [tolerance=±5% resistance=220 package=THT]
  R13 = Resistor [tolerance=±5% resistance=220 package=THT]
  R17 = Resistor [tolerance=±5% resistance=220 package=THT]
  R14 = Resistor [tolerance=±5% resistance=220 package=THT]
  R16 = Resistor [tolerance=±5% resistance=220 package=THT]
  R15 = Resistor [tolerance=±5% resistance=220 package=THT]
  R19 = Resistor [tolerance=±5% resistance=220 package=THT]
  R21 = Resistor [tolerance=±5% resistance=220 package=THT]
  R20 = Resistor [tolerance=±5% resistance=220 package=THT]
  R22 = Resistor [tolerance=±5% resistance=220 package=THT]
  R23 = Resistor [tolerance=±5% resistance=220 package=THT]
  R24 = Resistor [tolerance=±5% resistance=220 package=THT]
  R25 = Resistor [tolerance=±5% resistance=220 package=THT]
  R26 = Resistor [tolerance=±5% resistance=220 package=THT]
  R27 = Resistor [tolerance=±5% resistance=1k package=THT]
  R28 = Resistor [tolerance=±5% resistance=1k package=THT]
  R29 = Resistor [tolerance=±5% resistance=1k package=THT]
  RGB_LED_Matrix1 = RGB LED Matrix (8x8)
  U2 = Voltage Regulator - 5V [package="TO220 [THT]"]
  U1 = atmega328 [package=dip]
  J1 = female pin header, 3 pins [form="♀ (female)"]
  XTAL1 = Crystal [frequency="16 Mhz" package=THT]
  C8 = Capacitor [package=cap-pth-small2]
  C7 = Capacitor [package=cap-pth-small2]
  R34 = Resistor [tolerance=±5% resistance=330 package=THT]
  R36 = Resistor [tolerance=±5% resistance=330 package=THT]
  R33 = Resistor [tolerance=±5% resistance=330 package=THT]
  R37 = Resistor [tolerance=±5% resistance=330 package=THT]
  C17 = Tantalum Capacitor [capacitance=100nF package="100 mil [THT, tantalum]"]
  C13 = Tantalum Capacitor [capacitance=100nF package="100 mil [THT, tantalum]"]
  C14 = Tantalum Capacitor [capacitance=100nF package="100 mil [THT, tantalum]"]
  C16 = Tantalum Capacitor [capacitance=100nF package="100 mil [THT, tantalum]"]

nets:
  N1: U5.Q1, R2.Pin_1
  N2: U5.Q2, R3.Pin_1
  N3: U5.Q3, R4.Pin_1
  N4: U5.Q4, R5.Pin_1
  N5: U5.Q5, R6.Pin_1
  N6: U5.Q6, R7.Pin_1
  N7: U5.Q7, R8.Pin_1
  GND: U5.GND, U5.OE, U4.GND, U4.OE, U3.GND, U3.OE, U6.GND, U6.OE, VCC1.-, R31.Pin_1, S1.Pin_3, S1.Pin_4, C2.-, C1.-, S2.Pin_3, S2.Pin_4, C12.+, S3.Pin_3, S3.Pin_4, S4.Pin_3, S4.Pin_4, S5.Pin_3, S5.Pin_4, C15.+, S6.Pin_3, S6.Pin_4, S7.Pin_3, S7.Pin_4, R27.Pin_1, R28.Pin_1, R29.Pin_1, U2.GND, U1.GND, C8.2, C7.1, C17.+, C13.+, C14.+, C16.+
  N8: U5.Q7', R27.Pin_0
  VCC: U5.MR, U5.VCC, U4.MR, U4.VCC, U3.MR, U3.VCC, U6.MR, U6.VCC, LED1.anode, R30.Pin_1, C2.+, U2.output_voltage, U1.VCC, U1.AVCC, U1.AREF
  N9: U5.SH_CP, U4.SH_CP, U6.SH_CP, U1.A3
  N10: U5.ST_CP, U4.ST_CP, U6.ST_CP, U1.A4
  N11: U5.DS, U1.D13
  N12: U5.Q0, R1.Pin_1
  N13: U4.Q1, R12.Pin_1
  N14: U4.Q2, R18.Pin_1
  N15: U4.Q3, R13.Pin_1
  N16: U4.Q4, R17.Pin_1
  N17: U4.Q5, R14.Pin_1
  N18: U4.Q6, R16.Pin_1
  N19: U4.Q7, R15.Pin_1
  N20: U4.Q7', R28.Pin_0
  N21: U4.DS, U1.D11_(PWM)
  N22: U4.Q0, R9.Pin_1
  N23: U3.Q1, RGB_LED_Matrix1.Pin_31
  N24: U3.Q2, RGB_LED_Matrix1.Pin_30
  N25: U3.Q3, RGB_LED_Matrix1.Pin_29
  N26: U3.Q4, RGB_LED_Matrix1.Pin_20
  N27: U3.Q5, RGB_LED_Matrix1.Pin_19
  N28: U3.Q6, RGB_LED_Matrix1.Pin_18
  N29: U3.Q7, RGB_LED_Matrix1.Pin_17
  N30: U3.SH_CP, U1.A1
  N31: U3.ST_CP, U1.A2
  N32: U3.DS, U1.A0
  N33: U3.Q0, RGB_LED_Matrix1.Pin_32
  N34: U6.Q1, R25.Pin_0
  N35: U6.Q2, R24.Pin_0
  N36: U6.Q3, R23.Pin_0
  N37: U6.Q4, R22.Pin_0
  N38: U6.Q5, R20.Pin_0
  N39: U6.Q6, R21.Pin_0
  N40: U6.Q7, R19.Pin_0
  N41: U6.Q7', R29.Pin_0
  N42: U6.DS, U1.D12
  N43: U6.Q0, R26.Pin_0
  N44: VCC1.+, C1.+, U2.input_voltage
  N45: LED1.cathode, R31.Pin_0
  N46: R30.Pin_0, S1.Pin_1, S1.Pin_2, U1.RESET, J1.pin3
  N47: S2.Pin_1, S2.Pin_2, R32.Pin_1
  N48: R32.Pin_0, C12.-, U1.D6_(PWM)
  N49: S3.Pin_1, S3.Pin_2, R33.Pin_1
  N50: S4.Pin_1, S4.Pin_2, R34.Pin_1
  N51: R35.Pin_0, C15.-, U1.D3_(PWM)
  N52: R35.Pin_1, S5.Pin_1, S5.Pin_2
  N53: S6.Pin_1, S6.Pin_2, R36.Pin_1
  N54: S7.Pin_1, S7.Pin_2, R37.Pin_1
  N55: R1.Pin_0, RGB_LED_Matrix1.Pin_16
  N56: R2.Pin_0, RGB_LED_Matrix1.Pin_15
  N57: R3.Pin_0, RGB_LED_Matrix1.Pin_14
  N58: R4.Pin_0, RGB_LED_Matrix1.Pin_13
  N59: R5.Pin_0, RGB_LED_Matrix1.Pin_12
  N60: R6.Pin_0, RGB_LED_Matrix1.Pin_11
  N61: R7.Pin_0, RGB_LED_Matrix1.Pin_10
  N62: R8.Pin_0, RGB_LED_Matrix1.Pin_9
  N63: R9.Pin_0, RGB_LED_Matrix1.Pin_8
  N64: R12.Pin_0, RGB_LED_Matrix1.Pin_7
  N65: R18.Pin_0, RGB_LED_Matrix1.Pin_6
  N66: R13.Pin_0, RGB_LED_Matrix1.Pin_5
  N67: R17.Pin_0, RGB_LED_Matrix1.Pin_4
  N68: R14.Pin_0, RGB_LED_Matrix1.Pin_3
  N69: R16.Pin_0, RGB_LED_Matrix1.Pin_2
  N70: R15.Pin_0, RGB_LED_Matrix1.Pin_1
  N71: R19.Pin_1, RGB_LED_Matrix1.Pin_21
  N72: R21.Pin_1, RGB_LED_Matrix1.Pin_22
  N73: R20.Pin_1, RGB_LED_Matrix1.Pin_23
  N74: R22.Pin_1, RGB_LED_Matrix1.Pin_24
  N75: R23.Pin_1, RGB_LED_Matrix1.Pin_25
  N76: R24.Pin_1, RGB_LED_Matrix1.Pin_26
  N77: R25.Pin_1, RGB_LED_Matrix1.Pin_27
  N78: R26.Pin_1, RGB_LED_Matrix1.Pin_28
  N79: U1.D0_(RX), J1.pin2
  N80: U1.D1_(TX), J1.pin1
  N81: U1.D4, R33.Pin_0, C13.-
  N82: U1.XLAT1, XTAL1.pin_1, C8.1
  N83: U1.XLAT2, XTAL1.pin_0, C7.2
  N84: U1.D5_(PWM), R34.Pin_0, C14.-
  N85: U1.D7, R37.Pin_0, C17.-
  N86: U1.D8, R36.Pin_0, C16.-

custom parts:
  Pushbutton: A generic pushbutton.
  RGB LED Matrix (8x8): Description: This is a large sized, common anode, RGB LED Matrix. This is no supporting intelligence included with this part, so it needs an external driver, for example 4x 74LS595 shift registers and a supporting sketch. Documents: · Datasheet · Supporting info Example Projects: · None yet Dimensions: · 60.5 mm square
